// Logisim project ALU.circ as structural Verilog
module ALU (
  input  [31:0] A,
  input  [31:0] B,
  input  [4:0] Shift,
  input  [3:0] Codop,
  input  CarryIn,
  output [31:0] S,
  output [3:0] Flags
);

  wire [31:0] AandB, AandBBis, AfoisB, AorB, AplusB, AplusBplusCin, AplusBplusCinmoinsUn, AXorB, BandNotA,
       BmoinsA, BShiftArithmetic, BShiftLeft, BShiftRight, BShiftRotRight, not_1_out, notA, subtractor_1_out,
       ZeromoinsA;

  assign not_1_out = ~A;  // NOT_Gate not_1, 32 bits wide
  assign AandB = A & B;  // AND_Gate and_1, 32 bits wide
  assign AXorB = A ^ B;  // XOR_Gate xor_1, 32 bits wide
  Shifter #(.width(32)) shifter_1 (.in(B), .\dist (Shift), .out(BShiftLeft));
  Shifter #(.shift("lr"), .width(32)) shifter_2 (.in(B), .\dist (Shift), .out(BShiftRight));
  Shifter #(.shift("ar"), .width(32)) shifter_3 (.in(B), .\dist (Shift), .out(BShiftArithmetic));
  Adder #(.width(32)) adder_1 (.a(A), .b(B), .out(AplusBplusCin), .cin(CarryIn));  // open: cout
  Subtractor #(.width(32)) subtractor_1 (.a(A), .b(B), .out(subtractor_1_out), .bin(CarryIn));  // open: bout
  Shifter #(.shift("rr"), .width(32)) shifter_4 (.in(B), .\dist (Shift), .out(BShiftRotRight));
  assign AandBBis = A & B;  // AND_Gate and_2, 32 bits wide
  Subtractor #(.width(32)) subtractor_2 (.a({32{1'b0}}), .b(A), .out(ZeromoinsA));  // open: bin, bout
  Subtractor #(.width(32)) subtractor_3 (.a(B), .b(A), .out(BmoinsA));  // open: bin, bout
  Adder #(.width(32)) adder_2 (.a(A), .b(B), .out(AplusB));  // open: cin, cout
  assign AorB = A | B;  // OR_Gate or_1, 32 bits wide
  Multiplier #(.width(32)) multiplier_1 (.a(A), .b(B), .out(AfoisB));  // open: cin, cout
  assign BandNotA = not_1_out & B;  // AND_Gate and_3, 32 bits wide
  assign notA = ~A;  // NOT_Gate not_2, 32 bits wide
  Subtractor #(.width(32)) subtractor_4 (
    .a(subtractor_1_out), .b(32'h1), .out(AplusBplusCinmoinsUn));  // open: bin, bout
  Multiplexer #(.select(4), .width(32)) multiplexer_1 (
    .in0(AandB), .in1(AXorB), .in2(BShiftLeft), .in3(BShiftRight), .in4(BShiftArithmetic),
    .in5(AplusBplusCin), .in6(AplusBplusCinmoinsUn), .in7(BShiftRotRight), .in8(AandBBis), .in9(ZeromoinsA),
    .in10(BmoinsA), .in11(AplusB), .in12(AorB), .in13(AfoisB), .in14(BandNotA), .in15(notA),
    .out({Flags[3], S[30:0]}), .sel(Codop));  // open: en

  assign S[31] = Flags[3];

  // Other names for the same wires on the sheet: Cin = CarryIn; Sortie[31:0] = {Flags[3], S[30:0]}

  // Notes on the sheet:
  //   Note: for ROR, C = N
  //   Note 2: assume that shift > 0 for LSL and LSR
endmodule
